# Fritzing sketch snesToGameCube (saved by Fritzing 0.9.3b)
breadboards: 1

parts:
  Pro_Mini = Arduino Pro Mini (5V)
  R1 = Resistor [tolerance=±5% resistance=1k package=THT]
  SNES_IN = male pin header, 5 pins [form="♂ (male)"]
  GC_OUT = male pin header, 5 pins [form="♂ (male)"]
  Part4 = Logic Level Converter

nets:
  GND: Pro_Mini.GND, SNES_IN.pin5, GC_OUT.pin3, GC_OUT.pin4, Part4.GND
  N1: Pro_Mini.VCC, SNES_IN.pin4, GC_OUT.pin5, Part4.HV
  N2: Pro_Mini.MISO, SNES_IN.pin3
  N3: Pro_Mini.MOSI, SNES_IN.pin2
  N4: Pro_Mini.D10, SNES_IN.pin1
  N5: Pro_Mini.D8, Part4.TX_HV
  N6: R1.Pin_0, GC_OUT.pin2, Part4.LV
  N7: R1.Pin_1, GC_OUT.pin1, Part4.TX_LV

notes:
  latch
  clock
  data
  5v
  gnd
  SNES controller
  Gamecube connector
  3.3v
